# Fritzing sketch Schematic (saved by Fritzing 0.9.3b)
breadboards: 1

parts:
  S1 = Pushbutton [package="[THT]"]
  Parça1 = Arduino Uno (Rev3) - ICSP
  DI1 = 7-Segment LED Display [package=THT]
  R1 = Resistor [tolerance=±5% resistance=220 package="1206 [SMD]"]
  R2 = Resistor [tolerance=±5% resistance=220 package="1206 [SMD]"]

nets:
  N1: S1.Pin_1, S1.Pin_2, Parça1.GND
  N2: S1.Pin_3, S1.Pin_4, Parça1.D9_PWM, R2.Pin_1
  N3: Parça1.D8, DI1.cathodeG
  N4: Parça1.D2, DI1.cathodeE
  N5: Parça1.D3_PWM, DI1.cathodeD
  N6: Parça1.D4, DI1.cathodeC
  N7: Parça1.D5_PWM, DI1.cathodeB
  N8: Parça1.D6_PWM, DI1.cathodeA
  N9: Parça1.D7, DI1.cathodeF
  N10: Parça1.3V3, R1.Pin_0, R2.Pin_0
  N11: DI1.commAnode#2, R1.Pin_1
